// Logisim project oooo.circ as structural Verilog: 1 circuit, main circuit main
module main (
);

  wire and_1_out, and_2_out, and_3_out, and_4_out, and_5_out, and_6_out, and_7_out, and_8_out, and_9_out,
       and_10_out, and_11_out, and_12_out, and_13_out, and_14_out, and_15_out, and_16_out, and_17_out,
       and_18_out, and_19_out, and_20_out, and_21_out, and_22_out, and_23_out, and_24_out, and_25_out,
       and_26_out, and_27_out, and_28_out, and_29_out, and_30_out, and_31_out, and_32_out, clock_1_out,
       comparator_1_lt, decoder_1_out0, decoder_1_out1, decoder_1_out2, decoder_1_out3, decoder_1_out4,
       decoder_1_out5, decoder_1_out6, decoder_1_out7, decoder_1_out8, decoder_1_out9, decoder_1_out10,
       decoder_1_out11, decoder_1_out12, decoder_1_out13, decoder_1_out14, decoder_1_out15, decoder_1_out16,
       decoder_1_out17, decoder_1_out18, decoder_1_out19, decoder_1_out20, decoder_1_out21, decoder_1_out22,
       decoder_1_out23, decoder_1_out24, decoder_1_out25, decoder_1_out26, decoder_1_out27, decoder_1_out28,
       decoder_1_out29, decoder_1_out30, decoder_1_out31, not_2_out;
  wire [4:0] bit_extender_2_out, bit_extender_3_out, bit_extender_4_out;
  wire [23:0] bit_extender_5_out, bit_extender_6_out;
  wire [31:0] adder_1_out, adder_2_out, adder_3_out, and_33_out, bit_extender_1_out, bit_extender_7_out,
       divider_1_out, multiplexer_1_out, multiplexer_2_out, multiplexer_3_out, multiplexer_4_out,
       multiplexer_5_out, multiplexer_6_out, multiplexer_7_out, multiplier_1_out, not_1_out, or_1_out,
       ram_1_data, register_1_q, register_2_q, register_3_q, register_4_q, register_5_q, register_6_q,
       register_7_q, register_8_q, register_9_q, register_10_q, register_11_q, register_12_q, register_13_q,
       register_14_q, register_15_q, register_16_q, register_17_q, register_18_q, register_19_q,
       register_20_q, register_21_q, register_22_q, register_23_q, register_24_q, register_25_q,
       register_26_q, register_27_q, register_28_q, register_29_q, register_30_q, register_31_q,
       register_32_q, register_33_q, rom_1_data, shifter_1_out, shifter_2_out, shifter_3_out, undriven,
       xor_1_out;

  Decoder #(.select(5), .enable("false")) decoder_1 (
    .out0(decoder_1_out0), .out1(decoder_1_out1), .out2(decoder_1_out2), .out3(decoder_1_out3),
    .out4(decoder_1_out4), .out5(decoder_1_out5), .out6(decoder_1_out6), .out7(decoder_1_out7),
    .out8(decoder_1_out8), .out9(decoder_1_out9), .out10(decoder_1_out10), .out11(decoder_1_out11),
    .out12(decoder_1_out12), .out13(decoder_1_out13), .out14(decoder_1_out14), .out15(decoder_1_out15),
    .out16(decoder_1_out16), .out17(decoder_1_out17), .out18(decoder_1_out18), .out19(decoder_1_out19),
    .out20(decoder_1_out20), .out21(decoder_1_out21), .out22(decoder_1_out22), .out23(decoder_1_out23),
    .out24(decoder_1_out24), .out25(decoder_1_out25), .out26(decoder_1_out26), .out27(decoder_1_out27),
    .out28(decoder_1_out28), .out29(decoder_1_out29), .out30(decoder_1_out30), .out31(decoder_1_out31),
    .sel(rom_1_data[20:16]));
  and and_1 (and_1_out, decoder_1_out0, rom_1_data[29]);
  and and_2 (and_2_out, decoder_1_out1, rom_1_data[29]);
  and and_3 (and_3_out, decoder_1_out2, rom_1_data[29]);
  and and_4 (and_4_out, decoder_1_out3, rom_1_data[29]);
  and and_5 (and_5_out, decoder_1_out4, rom_1_data[29]);
  and and_6 (and_6_out, decoder_1_out5, rom_1_data[29]);
  and and_7 (and_7_out, decoder_1_out6, rom_1_data[29]);
  and and_8 (and_8_out, decoder_1_out7, rom_1_data[29]);
  and and_9 (and_9_out, decoder_1_out8, rom_1_data[29]);
  and and_10 (and_10_out, decoder_1_out9, rom_1_data[29]);
  and and_11 (and_11_out, decoder_1_out10, rom_1_data[29]);
  and and_12 (and_12_out, decoder_1_out11, rom_1_data[29]);
  and and_13 (and_13_out, decoder_1_out12, rom_1_data[29]);
  and and_14 (and_14_out, decoder_1_out13, rom_1_data[29]);
  and and_15 (and_15_out, decoder_1_out14, rom_1_data[29]);
  and and_16 (and_16_out, decoder_1_out15, rom_1_data[29]);
  and and_17 (and_17_out, decoder_1_out16, rom_1_data[29]);
  and and_18 (and_18_out, decoder_1_out17, rom_1_data[29]);
  and and_19 (and_19_out, decoder_1_out18, rom_1_data[29]);
  and and_20 (and_20_out, decoder_1_out19, rom_1_data[29]);
  and and_21 (and_21_out, decoder_1_out20, rom_1_data[29]);
  and and_22 (and_22_out, decoder_1_out21, rom_1_data[29]);
  and and_23 (and_23_out, decoder_1_out22, rom_1_data[29]);
  and and_24 (and_24_out, decoder_1_out23, rom_1_data[29]);
  and and_25 (and_25_out, decoder_1_out24, rom_1_data[29]);
  and and_26 (and_26_out, decoder_1_out25, rom_1_data[29]);
  and and_27 (and_27_out, decoder_1_out26, rom_1_data[29]);
  and and_28 (and_28_out, decoder_1_out27, rom_1_data[29]);
  and and_29 (and_29_out, decoder_1_out28, rom_1_data[29]);
  and and_30 (and_30_out, decoder_1_out29, rom_1_data[29]);
  and and_31 (and_31_out, decoder_1_out30, rom_1_data[29]);
  and and_32 (and_32_out, decoder_1_out31, rom_1_data[29]);
  Register #(.width(32)) register_1 (
    .D(multiplexer_1_out), .en(and_1_out), .Q(register_1_q), .clk(clock_1_out));  // open: clr
  Register #(.width(32)) register_2 (
    .D(multiplexer_1_out), .en(and_2_out), .Q(register_2_q), .clk(clock_1_out));  // open: clr
  Register #(.width(32)) register_3 (
    .D(multiplexer_1_out), .en(and_3_out), .Q(register_3_q), .clk(clock_1_out));  // open: clr
  Register #(.width(32)) register_4 (
    .D(multiplexer_1_out), .en(and_4_out), .Q(register_4_q), .clk(clock_1_out));  // open: clr
  Register #(.width(32)) register_5 (
    .D(multiplexer_1_out), .en(and_5_out), .Q(register_5_q), .clk(clock_1_out));  // open: clr
  Register #(.width(32)) register_6 (
    .D(multiplexer_1_out), .en(and_6_out), .Q(register_6_q), .clk(clock_1_out));  // open: clr
  Register #(.width(32)) register_7 (
    .D(multiplexer_1_out), .en(and_7_out), .Q(register_7_q), .clk(clock_1_out));  // open: clr
  Register #(.width(32)) register_8 (
    .D(multiplexer_1_out), .en(and_8_out), .Q(register_8_q), .clk(clock_1_out));  // open: clr
  Register #(.width(32)) register_9 (
    .D(multiplexer_1_out), .en(and_9_out), .Q(register_9_q), .clk(clock_1_out));  // open: clr
  Register #(.width(32)) register_10 (
    .D(multiplexer_1_out), .en(and_10_out), .Q(register_10_q), .clk(clock_1_out));  // open: clr
  Register #(.width(32)) register_11 (
    .D(multiplexer_1_out), .en(and_11_out), .Q(register_11_q), .clk(clock_1_out));  // open: clr
  Register #(.width(32)) register_12 (
    .D(multiplexer_1_out), .en(and_12_out), .Q(register_12_q), .clk(clock_1_out));  // open: clr
  Register #(.width(32)) register_13 (
    .D(multiplexer_1_out), .en(and_13_out), .Q(register_13_q), .clk(clock_1_out));  // open: clr
  Register #(.width(32)) register_14 (
    .D(multiplexer_1_out), .en(and_14_out), .Q(register_14_q), .clk(clock_1_out));  // open: clr
  Register #(.width(32)) register_15 (
    .D(multiplexer_1_out), .en(and_15_out), .Q(register_15_q), .clk(clock_1_out));  // open: clr
  Register #(.width(32)) register_16 (
    .D(multiplexer_1_out), .en(and_16_out), .Q(register_16_q), .clk(clock_1_out));  // open: clr
  Register #(.width(32)) register_17 (
    .D(multiplexer_1_out), .en(and_17_out), .Q(register_17_q), .clk(clock_1_out));  // open: clr
  Register #(.width(32)) register_18 (
    .D(multiplexer_1_out), .en(and_18_out), .Q(register_18_q), .clk(clock_1_out));  // open: clr
  Register #(.width(32)) register_19 (
    .D(multiplexer_1_out), .en(and_19_out), .Q(register_19_q), .clk(clock_1_out));  // open: clr
  Register #(.width(32)) register_20 (
    .D(multiplexer_1_out), .en(and_20_out), .Q(register_20_q), .clk(clock_1_out));  // open: clr
  Register #(.width(32)) register_21 (
    .D(multiplexer_1_out), .en(and_21_out), .Q(register_21_q), .clk(clock_1_out));  // open: clr
  Register #(.width(32)) register_22 (
    .D(multiplexer_1_out), .en(and_22_out), .Q(register_22_q), .clk(clock_1_out));  // open: clr
  Register #(.width(32)) register_23 (
    .D(multiplexer_1_out), .en(and_23_out), .Q(register_23_q), .clk(clock_1_out));  // open: clr
  Register #(.width(32)) register_24 (
    .D(multiplexer_1_out), .en(and_24_out), .Q(register_24_q), .clk(clock_1_out));  // open: clr
  Register #(.width(32)) register_25 (
    .D(multiplexer_1_out), .en(and_25_out), .Q(register_25_q), .clk(clock_1_out));  // open: clr
  Register #(.width(32)) register_26 (
    .D(multiplexer_1_out), .en(and_26_out), .Q(register_26_q), .clk(clock_1_out));  // open: clr
  Register #(.width(32)) register_27 (
    .D(multiplexer_1_out), .en(and_27_out), .Q(register_27_q), .clk(clock_1_out));  // open: clr
  Register #(.width(32)) register_28 (
    .D(multiplexer_1_out), .en(and_28_out), .Q(register_28_q), .clk(clock_1_out));  // open: clr
  Register #(.width(32)) register_29 (
    .D(multiplexer_1_out), .en(and_29_out), .Q(register_29_q), .clk(clock_1_out));  // open: clr
  Register #(.width(32)) register_30 (
    .D(multiplexer_1_out), .en(and_30_out), .Q(register_30_q), .clk(clock_1_out));  // open: clr
  Register #(.width(32)) register_31 (
    .D(multiplexer_1_out), .en(and_31_out), .Q(register_31_q), .clk(clock_1_out));  // open: clr
  Register #(.width(32)) register_32 (
    .D(multiplexer_1_out), .en(and_32_out), .Q(register_32_q), .clk(clock_1_out));  // open: clr
  Multiplexer #(.width(32), .enable("false")) multiplexer_1 (
    .in0(multiplexer_7_out), .in1(ram_1_data), .out(multiplexer_1_out), .sel(rom_1_data[31]));
  Multiplexer #(.select(5), .width(32), .enable("false")) multiplexer_2 (
    .in0(register_1_q), .in1(register_2_q), .in2(register_3_q), .in3(register_4_q), .in4(register_5_q),
    .in5(register_6_q), .in6(register_7_q), .in7(register_8_q), .in8(register_9_q), .in9(register_10_q),
    .in10(register_11_q), .in11(register_12_q), .in12(register_13_q), .in13(register_14_q),
    .in14(register_15_q), .in15(register_16_q), .in16(register_17_q), .in17(register_18_q),
    .in18(register_19_q), .in19(register_20_q), .in20(register_21_q), .in21(register_22_q),
    .in22(register_23_q), .in23(register_24_q), .in24(register_25_q), .in25(register_26_q),
    .in26(register_27_q), .in27(register_28_q), .in28(register_29_q), .in29(register_30_q),
    .in30(register_31_q), .in31(register_32_q), .out(multiplexer_2_out), .sel(rom_1_data[25:21]));
  Clock clock_1 (.out(clock_1_out));
  assign bit_extender_1_out = {{22{1'b0}}, rom_1_data[15:6]};  // Bit_Extender bit_extender_1
  assign not_1_out = ~bit_extender_1_out;  // NOT_Gate not_1, 32 bits wide
  Bit_Extender #(.in_width(32), .out_width(5)) bit_extender_2 (.in(multiplexer_2_out), .out(bit_extender_2_out));
  Bit_Extender #(.in_width(32), .out_width(5)) bit_extender_3 (.in(multiplexer_2_out), .out(bit_extender_3_out));
  Bit_Extender #(.in_width(32), .out_width(5)) bit_extender_4 (.in(multiplexer_2_out), .out(bit_extender_4_out));
  Bit_Extender #(.in_width(32), .out_width(24)) bit_extender_5 (.in(multiplexer_7_out), .out(bit_extender_5_out));
  Bit_Extender #(.in_width(32), .out_width(24)) bit_extender_6 (.in(register_33_q), .out(bit_extender_6_out));
  Register #(.width(32)) register_33 (.D(adder_2_out), .Q(register_33_q), .clk(clock_1_out));  // open: en, clr
  Adder #(.width(32)) adder_1 (.a(not_1_out), .b(undriven), .out(adder_1_out));  // open: cin, cout
  Multiplier #(.width(32)) multiplier_1 (
    .a(multiplexer_2_out), .b(bit_extender_1_out), .out(multiplier_1_out));  // open: cin, cout
  Divider #(.width(32)) divider_1 (
    .a(multiplexer_2_out), .b(bit_extender_1_out), .out(divider_1_out));  // open: upper, rem
  Comparator #(.width(32)) comparator_1 (
    .a(multiplexer_2_out), .b(bit_extender_1_out), .lt(comparator_1_lt));  // open: gt, eq
  assign xor_1_out = multiplexer_2_out ^ bit_extender_1_out;  // XOR_Gate xor_1, 32 bits wide
  Shifter #(.width(32), .shift("lr")) shifter_1 (
    .in(multiplexer_2_out), .\dist (bit_extender_2_out), .out(shifter_1_out));
  Shifter #(.width(32)) shifter_2 (.in(multiplexer_2_out), .\dist (bit_extender_3_out), .out(shifter_2_out));
  Shifter #(.width(32)) shifter_3 (.in(multiplexer_2_out), .\dist (bit_extender_4_out), .out(shifter_3_out));
  assign or_1_out = multiplexer_2_out | bit_extender_1_out;  // OR_Gate or_1, 32 bits wide
  assign and_33_out = multiplexer_2_out & bit_extender_1_out;  // AND_Gate and_33, 32 bits wide
  Adder #(.width(32)) adder_2 (.a(register_33_q), .b(undriven), .out(adder_2_out));  // open: cin, cout
  Multiplexer #(.width(32), .enable("false")) multiplexer_3 (
    .in0(not_1_out), .in1(adder_1_out), .out(multiplexer_3_out), .sel(rom_1_data[3]));
  assign bit_extender_7_out = {{31{1'b0}}, comparator_1_lt};  // Bit_Extender bit_extender_7
  Multiplexer #(.width(32), .enable("false")) multiplexer_4 (
    .in0(shifter_2_out), .in1(shifter_3_out), .out(multiplexer_4_out), .sel(rom_1_data[3]));
  RAM #(.addrWidth(24), .dataWidth(32), .bus("separate")) ram_1 (
    .addr(bit_extender_5_out), .din(multiplexer_2_out), .data(ram_1_data), .str(rom_1_data[30]),
    .clk(clock_1_out), .ld(not_2_out));  // open: sel, clr
  not not_2 (not_2_out, rom_1_data[30]);
  ROM #(.addrWidth(24), .dataWidth(32)) rom_1 (.addr(bit_extender_6_out), .data(rom_1_data));  // open: sel
  Adder #(.width(32)) adder_3 (.a(multiplexer_2_out), .b(multiplexer_3_out), .out(adder_3_out));  // open: cin, cout
  Multiplexer #(.select(3), .width(32), .enable("false")) multiplexer_5 (
    .in0(multiplier_1_out), .in1(divider_1_out), .in2(bit_extender_7_out), .in3(xor_1_out),
    .in4(shifter_1_out), .in5(multiplexer_4_out), .in6(or_1_out), .in7(and_33_out), .out(multiplexer_5_out),
    .sel(rom_1_data[2:0]));
  Multiplexer #(.width(32), .enable("false")) multiplexer_6 (
    .in0(adder_3_out), .in1(multiplexer_5_out), .out(multiplexer_6_out), .sel(rom_1_data[4]));
  Multiplexer #(.width(32), .enable("false")) multiplexer_7 (
    .in0(multiplexer_6_out), .in1(bit_extender_1_out), .out(multiplexer_7_out), .sel(rom_1_data[5]));
endmodule
